// Digital circuit circuito.dig as structural Verilog
module circuito (
  input  [31:0] A_i,
  input  [31:0] B_i,
  input  mode_i,
  input  [1:0] vecSize_i,
  output [31:0] S_o
);

  SomadorSubtratorVetorial #(.applicationType("GHDL"), .CodeFile("/home/brito/Downloads/arqcomp/modulo.vhd")) u_SomadorSubtratorVetorial (
    .A_i(A_i), .B_i(B_i), .mode_i(mode_i), .vecSize_i(vecSize_i), .S_o(S_o));
endmodule

/* Test case Teste:
A_i B_i mode_i vecSize_i S_o

0x00000111   0x00000222   0      3                 0x00000333
0x00000888   0x00000333   1      3                 0x00000555
0x40005000   0x00020007   0      3                 0x40025007
0x01110222   0x03330444   0      2                 0x04440666
0x000C000D   0x0001000A   1      2                 0x000B0003
0xFFEE0005   0x00220005   0      2                 0x0010000A
0x20304050   0x05060708   0      1                 0x25364758
0xDDBB9977   0x11111111   1      1                 0x0CCAA8866
0x24681357   0x11112222   0      0                 0x35793579
0xABCDEF98   0x22222222   1      0                 0x89ABCD76
0xAAAAAAAA   0x66666666   0      0                 0x00000000
*/
